# Fritzing sketch breadboard-psu (saved by Fritzing 0.8.3b)
circuit board: 2.46474cm x 6.4723cm
breadboards: 1

parts:
  U2 = mystery part, 6 pins [chip_label=? spacing=100mil]
  U3 = mystery part, 6 pins [chip_label=? spacing=100mil]
  U4 = Voltage Regulator - 5V [package="TO220 [THT]"]
  C1 = Ceramic Capacitor [capacitance=100nF package="100 mil [THT, multilayer]"]
  D1 = Rectifier Diode [part_number=1N4001 package="300 mil [THT]"]
  U5 = mystery part, 3 pins [chip_label=? spacing=300mil]
  LED1 = LED - 5mm [color="Red (633nm)" package="5 mm [THT]"]
  R1 = Resistor [tolerance=±5% resistance=1k package=THT]
  U7 = mystery part, 9 pins [chip_label=? spacing=300mil]
  U8 = mystery part, 3 pins [chip_label=? spacing=300mil]
  VCC1 = Battery
  LED2 = LED - 5mm [color="Green (570nm)" package="5 mm [THT]"]
  R2 = Resistor [tolerance=±5% resistance=1k package=THT]
  U6 = Voltage Regulator - 3.3V [package="TO220 [THT]"]
  U9 = mystery part, 1 pin [chip_label=? spacing=300mil]
  U10 = mystery part, 2 pins [chip_label=? spacing=300mil]
  C2 = Ceramic Capacitor [capacitance=100nF package="100 mil [THT, multilayer]"]
  C3 = Electrolytic Capacitor [capacitance=1µF package="100 mil [THT, electrolytic]"]
  C4 = Electrolytic Capacitor [capacitance=1µF package="100 mil [THT, electrolytic]"]
  U11 = mystery part, 2 pins [chip_label=? spacing=300mil]
  U12 = mystery part, 2 pins [chip_label=? spacing=300mil]
  U13 = mystery part, 2 pins [chip_label=? spacing=300mil]

nets:
  N1: U2.pin1, U2.pin2, U2.pin3, U4.output_voltage, C1.1, U5.pin3, R1.Pin_0, U7.pin1, U7.pin2, U7.pin3, U7.pin4, U7.pin5, U7.pin6, U7.pin7, U7.pin8, U7.pin9, U8.pin1, C3.+, U11.pin2
  GND: U2.pin4, U2.pin5, U2.pin6, U3.pin4, U3.pin5, U3.pin6, U4.GND, C1.0, U5.pin2, LED1.cathode, VCC1.+, LED2.cathode, U6.GND, U9.pin1, C2.0, C3.-, C4.-, U12.pin1, U12.pin2, U13.pin1
  N2: U3.pin1, U3.pin2, U3.pin3, U8.pin2, R2.Pin_0
  N3: U4.input_voltage, D1.cathode, U5.pin1, U6.input_voltage, U10.pin1, U10.pin2, C2.1, U13.pin2
  N4: D1.anode, VCC1.-
  N5: LED1.anode, R1.Pin_1
  N6: U8.pin3, U6.output_voltage, C4.+
  N7: LED2.anode, R2.Pin_1

notes:
  PSU
